# Fritzing sketch Helicopter Prototype Circuit (saved by Fritzing 0.9.2b)
breadboards: 1

parts:
  Part1 = Arduino Uno (Rev3)
  R5 = Resistor [tolerance=±5% resistance=220 package=THT]
  R6 = Resistor [tolerance=±5% resistance=220 package=THT]
  LED1 = LED - 5mm [color="Blue (430nm)" package="5 mm [THT]"]
  R7 = Resistor [tolerance=±5% resistance=220 package=THT]
  R8 = Resistor [tolerance=±5% resistance=220 package=THT]
  C3 = Ceramic Capacitor [capacitance=10pF package="100 mil [THT, multilayer]"]
  C4 = Ceramic Capacitor [capacitance=100nF package="100 mil [THT, multilayer]"]
  R9 = Resistor [tolerance=±5% resistance=220 package=THT]
  J1 = female pin header, 2 pins [form="♀ (female)"]
  J2 = female pin header, 8 pins [form="♀ (female)"]
  J3 = single row smd female pin header, 6 pins [form="♀ (female)"]
  J5 = female pin header, 2 pins [form="♀ (female)"]
  J7 = female pin header, 2 pins [form="♀ (female)"]
  J8 = female pin header, 2 pins [form="♀ (female)"]
  J10 = female pin header, 2 pins [form="♀ (female)"]
  IC11 = IC, DIP package, 16 pins [chip_label=ADC]
  IC12 = IC, DIP package, 14 pins [chip_label=DAC]
  IC13 = IC, DIP package, 14 pins [chip_label="QUAD XOR"]
  IC14 = IC, DIP package, 14 pins [chip_label="QUAD OR"]
  J11 = female pin header, 2 pins [form="♀ (female)"]
  J12 = female pin header, 2 pins [form="♀ (female)"]
  J13 = single row smd female pin header, 5 pins [form="♀ (female)"]

nets:
  N1: Part1.D9_PWM, J2.pin4, IC11.pin2
  N2: Part1.D10_PWM/SS, J2.pin5, IC12.pin3
  N3: Part1.D11_PWM/MOSI, J2.pin8, IC11.pin3, IC12.pin5
  N4: Part1.D12/MISO, J2.pin6, IC11.pin4
  N5: Part1.D13/SCK, J2.pin7, IC11.pin5, IC12.pin4
  N6: Part1.D0/RX, J2.pin1, J3.pin4
  N7: Part1.D1/TX, R5.Pin_0, J2.pin2
  N8: Part1.D2, IC14.pin10, J11.pin1, J11.pin2
  N9: Part1.D4, R7.Pin_1, J8.pin1, J10.pin1, IC13.pin12
  N10: Part1.D5_PWM, R8.Pin_1, J8.pin2, J10.pin2, IC13.pin9
  N11: Part1.D6_PWM, LED1.cathode, J2.pin3
  N12: Part1.5V, J1.pin1, J3.pin2, J5.pin1, J7.pin1, IC11.pin7, IC11.pin8, IC12.pin1, IC12.pin9, IC12.pin11, IC12.pin13, IC13.pin7, IC14.pin7, J13.pin2, J13.pin4
  N13: Part1.GND, R6.Pin_1, C3.0, C4.0, R9.Pin_1, J1.pin2, J3.pin3, J5.pin2, J7.pin2, IC11.pin1, IC11.pin6, IC12.pin8, IC12.pin12, IC13.pin14, IC14.pin14, J13.pin3
  N14: R5.Pin_1, R9.Pin_0, J3.pin5
  N15: R6.Pin_0, LED1.anode
  N16: R7.Pin_0, C3.1, IC13.pin11
  N17: R8.Pin_0, C4.1, IC13.pin8
  N18: IC11.pin10, J12.pin1, J12.pin2
  N19: IC12.pin10, J13.pin5
  N20: IC12.pin14, J13.pin1
  N21: IC13.pin10, IC14.pin8
  N22: IC13.pin13, IC14.pin9

notes:
  Y=In, G=Out, B=Misc.,O=DIn
  Relative to Breadboard:
  To encoder
  To potentiometer
  JY-MCU Header
  To motor driver
